# Fritzing sketch Arduino-RF434MHz (saved by Fritzing 0.8.7b)
breadboards: 1

parts:
  U1 = RF-LINK_RX [package=rf-link_rx]
  U2 = RF-LINK_TX [package=rf-link_tx]
  Part1 = Arduino Ethernet Shield (Rev3)
  R1 = Photocell (LDR) [package=THT]
  R2 = Resistor [tolerance=±5% resistance=10k package=THT]

nets:
  GND: U1.GND, U2.GND, Part1.GND, R2.Pin_1
  N1: U1.DATA, Part1.D2
  +5V: U1.+5V, U2.+5V, Part1.5V, R1.pin_1
  N2: U2.DATA, Part1.D7
  N3: Part1.A0, R1.pin_0, R2.Pin_0
